# Fritzing sketch schema (saved by Fritzing 0.9.9b)
circuit board: 8.46667cm x 5.64444cm
breadboards: 1

parts:
  Composant1 = Arduino Nano (Rev3.0)
  S1 = Pushbutton [package="[THT]"]
  S2 = Pushbutton [package="[THT]"]
  SPKR1 = Loudspeaker
  Q1 = NPN-Transistor [part_number="BC 549 B" package="TO92 [THT]"]

nets:
  GND: Composant1.GND, S1.Pin_1, S1.Pin_2, S2.Pin_1, S2.Pin_2, SPKR1.pin1
  N1: Composant1.A1, S2.Pin_3, S2.Pin_4
  N2: Composant1.A0, S1.Pin_3, S1.Pin_4
  N3: Composant1.3V3, Q1.C
  N4: Composant1.D13/SCK, Q1.B
  N5: SPKR1.pin2, Q1.E
