# Fritzing sketch led6 (saved by Fritzing 0.9.2b)
breadboards: 1

parts:
  R1 = Resistor [tolerance=±5% resistance=6.8k package=THT]
  R3 = Resistor [tolerance=±5% resistance=6.8k package=THT]
  R5 = Resistor [tolerance=±5% resistance=6.8k package=THT]
  LED2' = LED - 5mm [color="Red (633nm)" package="5 mm [THT]"]
  LED2 = LED - 5mm [color="Red (633nm)" package="5 mm [THT]"]
  LED1' = LED - 5mm [color="Red (633nm)" package="5 mm [THT]"]
  LED3 = LED - 5mm [color="Red (633nm)" package="5 mm [THT]"]
  LED1 = LED - 5mm [color="Red (633nm)" package="5 mm [THT]"]
  R7 = Resistor [tolerance=±5% resistance=100 package=THT]
  R8 = Resistor [tolerance=±5% resistance=100 package=THT]
  R9 = Resistor [tolerance=±5% resistance=100 package=THT]
  LED3' = LED - 5mm [color="Red (633nm)" package="5 mm [THT]"]
  Q1 = PNP-Transistor [package="TO92 [THT]"]
  Q3 = PNP-Transistor [package="TO92 [THT]"]
  LED1a = LED - 5mm [color="Red (633nm)" package="5 mm [THT]"]
  LED3a = LED - 5mm [color="Red (633nm)" package="5 mm [THT]"]
  LED2a = LED - 5mm [color="Red (633nm)" package="5 mm [THT]"]
  LED1b = LED - 5mm [color="Red (633nm)" package="5 mm [THT]"]
  LED2b = LED - 5mm [color="Red (633nm)" package="5 mm [THT]"]
  LED3b = LED - 5mm [color="Red (633nm)" package="5 mm [THT]"]
  R10 = Resistor [tolerance=±5% resistance=100 package=THT]
  R11 = Resistor [tolerance=±5% resistance=100 package=THT]
  R12 = Resistor [tolerance=±5% resistance=100 package=THT]
  Q5 = PNP-Transistor [package="TO92 [THT]"]
  Q2 = NPN-Transistor [package="TO92 [THT]"]
  Q4 = NPN-Transistor [package="TO92 [THT]"]
  Q6 = NPN-Transistor [package="TO92 [THT]"]

nets:
  N1: R1.Pin_0, Q1.B, Q2.B
  N2: R3.Pin_0, Q3.B, Q4.B
  N3: R5.Pin_0, Q5.B, Q6.B
  N4: LED2'.cathode, LED2.anode, LED1'.anode, LED1.cathode, R8.Pin_0
  N5: LED2'.anode, LED2.cathode, LED3.anode, R9.Pin_1, LED3'.cathode
  N6: LED1'.cathode, LED3.cathode, LED1.anode, R7.Pin_0, LED3'.anode
  N7: Q1.E, R10.Pin_1, Q2.E
  GND: Q1.C, Q3.C, Q5.C
  N8: Q3.E, R11.Pin_1, Q4.E
  N9: LED1a.cathode, LED2a.anode, LED1b.anode, LED2b.cathode, R10.Pin_0
  N10: LED1a.anode, LED3a.cathode, LED1b.cathode, LED3b.anode, R12.Pin_0
  N11: LED3a.anode, LED2a.cathode, LED2b.anode, LED3b.cathode, R11.Pin_0
  N12: R12.Pin_1, Q5.E, Q6.E
  5V: Q2.C, Q4.C, Q6.C

notes:
  A
  B
  C
  A'
  B'
  C'
